# Fritzing sketch Interactive_Demoscene (saved by Fritzing 0.9.5d)
breadboards: 1

parts:
  Composant1 = Arduino Uno (Rev3)
  Composant2 = Thumb Joystick
  LCD1 = TFT 1.8 inch 160x128 no SD

nets:
  N1: Composant1.A0, Composant2.VERT
  N2: Composant1.A1, Composant2.HORZ
  N3: Composant1.D8, LCD1.pin4
  N4: Composant1.D9_PWM, LCD1.pin_5
  N5: Composant1.D10_PWM/SS, LCD1.pin3
  N6: Composant1.D11_PWM/MOSI, LCD1.pin_6
  N7: Composant1.D13/SCK, LCD1.pin_7
  N8: Composant1.D4, Composant2.SEL
  N9: Composant1.3V3, LCD1.pin_1, LCD1.pin_8
  5V: Composant1.5V, Composant2.VCC
  GND: Composant1.GND, Composant2.GND, LCD1.pin2

notes:
  Écran
  https://wiki.dfrobot.com/2.0_Inches_320_240_IPS_TFT_LCD_Display_with_MicroSD_Card_Breakout_SKU_DFR0664#Connection%20Diagram
  PIN 13 -> CK
  PIN 12 -> SI
  PIN 11 -> SO
  5V -> V
  GND -> G
  PIN 7 -> CS
  PIN 6 -> RT
  PIN 5 -> DC

custom parts:
  TFT 1.8 inch 160x128 no SD: This is a generic 1.8 tft spi lcd display available on ebay and others. The 1.8" display has 128x160 color pixels and in this version pin names in breadboard (unlike the real board) and with no SD interface.
